# Fritzing sketch Rasp-tempsensor (saved by Fritzing 0.8.7b)
circuit board: 8.46667cm x 5.64444cm
breadboards: 1

parts:
  Pi1 = Adafruit Pi Cobbler
  AM1 = AM2302 Humidity and Temperature Sensor
  DHT1 = DHT22 Humidity and Temperature Sensor
  R2 = Resistor [tolerance=±5% resistance=472 package=THT]

nets:
  VDD: Pi1.3V3, AM1.VDD, DHT1.VDD, R2.Pin_0
  GND: Pi1.GND, Pi1.#4, AM1.DATA, AM1.GND, DHT1.GND
  N1: Pi1.#17, DHT1.DATA, R2.Pin_1

custom parts:
  Adafruit Pi Cobbler: Adafruit Pi Cobbler GPIO Breakout for Raspberry Pi
